// Logisim project projet vide.circ as structural Verilog: 13 circuits, main circuit main
module main (
  input  Reset,
  input  ResetRAM
);

  wire CALL, Clock, Clock_out, Cond, CTRL, Exec, Fetch, getcst_1_imm, Load, ramctrl_1_memload,
       ramctrl_1_memstore, RET, Store, WriteReg;
  wire [2:0] GetOp;
  wire [15:0] Addr, alu_1_output, getcst_1_cst, JMP_Address, MemIN, PC, R0, R1, R2, R3, R4, R5, R6, R7,
       registres_1_out_sr2, SR1Out;
  wire [31:0] bit_extender_1_out, IR, MemOUT;

  Clock u_Clock (.out(Clock_out));
  Seq seq_1 (.ClockOrig(Clock_out), .reset(Reset), .Fetch(Fetch), .Exec(Exec), .Clock(Clock));
  LED led_1 (.in(Clock_out));
  RegPC regpc_1 (
    .JMP_Address(JMP_Address), .Cond(Cond), .CTRL(CTRL), .Clock(Exec), .Reset(Reset), .PC(PC), .CALL(CALL),
    .RET(RET));  // open: Arith
  // Probe on PC
  GetAddr getaddr_1 (.PC(PC), .Addr(Addr), .Fetch(Fetch), .Load(Load), .Store(Store));
  // Probe on Addr
  LED led_2 (.in(Fetch));
  LED led_3 (.in(Exec));
  // Probe on MemIN
  assign bit_extender_1_out = {{16{MemIN[15]}}, MemIN};  // Bit_Extender bit_extender_1
  // Probe on PC
  // Probe on IR
  DecodeIR decodeir_1 (
    .WriteReg(WriteReg), .IR(IR), .Load(Load), .GetOp(GetOp), .JMPAddress(JMP_Address), .Store(Store),
    .CTRL(CTRL), .CALL(CALL), .RET(RET));
  RamCtrl ramctrl_1 (
    .Store(Store), .Fetch(Fetch), .Exec(Exec), .Load(Load), .MemStore(ramctrl_1_memstore),
    .MemLoad(ramctrl_1_memload), .Clock(Clock));
  // Probe on MemOUT
  RAM #(.addrWidth(16), .dataWidth(32), .bus("separate")) ram_1 (
    .addr(Addr), .din(bit_extender_1_out), .data(MemOUT), .str(ramctrl_1_memstore), .clk(ramctrl_1_memstore),
    .ld(ramctrl_1_memload), .clr(ResetRAM));  // open: sel
  // Probe on R0
  // Probe on R3
  // Probe on R6
  Register #(.width(32), .trigger("falling")) RegIR (.D(MemOUT), .Q(IR), .clk(Fetch), .clr(Reset));  // open: en
  // Probe on R1
  // Probe on R4
  // Probe on R7
  // Probe on IR
  // Probe on R2
  // Probe on R5
  // Probe on IR[8:6]
  // Probe on IR[11:9]
  // Probe on IR[14:12]
  // Probe on getcst_1_cst
  GetCst getcst_1 (.IR(IR), .Cst(getcst_1_cst), .Imm(getcst_1_imm));
  Registres registres_1 (
    .SR1(IR[11:9]), .IN(alu_1_output), .SR2(IR[14:12]), .WriteReg(WriteReg), .DR(IR[8:6]), .OUT_SR1(SR1Out),
    .OUT_SR2(registres_1_out_sr2), .OUT_DR(MemIN), .R0(R0), .R1(R1), .R2(R2), .R3(R3), .R4(R4), .R5(R5),
    .R6(R6), .R7(R7), .Reset(Reset), .Clock(Exec));
  // Probe on SR1Out
  // Probe on registres_1_out_sr2
  ALU alu_1 (
    .Imm(getcst_1_imm), .e2(GetOp), .Input1(SR1Out), .Input2(registres_1_out_sr2), .Cst(getcst_1_cst),
    .Output(alu_1_output));
  // Probe on alu_1_output
  // Probe on R0
  // Probe on R1
  // Probe on R2
  // Probe on R3
  // Probe on R4
  // Probe on R5
  // Probe on R6
  // Probe on R7
  // Probe on alu_1_output
  Cond_Crtl cond_crtl_1 (.GetOp(GetOp), .Cond(Cond), .Reg1(MemIN), .Reg2(SR1Out));

  // Notes on the sheet:
  //   RAM
endmodule

module ALU (
  input  [15:0] Input1,
  input  [15:0] Input2,
  input  [15:0] Cst,
  input  Imm,
  input  [2:0] e2,
  output [15:0] Output
);

  wire [15:0] adder_1_out, and_1_out, mod_1_res, multiplexer_1_out, or_1_out, shifter_1_out, shifter_2_out,
       subtractor_1_out, xor_1_out;

  Multiplexer #(.width(16), .enable("false")) multiplexer_1 (
    .in0(Input2), .in1(Cst), .out(multiplexer_1_out), .sel(Imm));
  assign or_1_out = Input1 | multiplexer_1_out;  // OR_Gate or_1, 16 bits wide
  assign and_1_out = Input1 & multiplexer_1_out;  // AND_Gate and_1, 16 bits wide
  Mod mod_1 (.Input1(Input1), .Input1_2(multiplexer_1_out), .Res(mod_1_res));
  Shifter #(.width(16), .shift("lr")) shifter_1 (.in(Input1), .\dist (multiplexer_1_out[3:0]), .out(shifter_1_out));
  Shifter #(.width(16)) shifter_2 (.in(Input1), .\dist (multiplexer_1_out[3:0]), .out(shifter_2_out));
  assign xor_1_out = Input1 ^ multiplexer_1_out;  // XOR_Gate xor_1, 16 bits wide
  Subtractor #(.width(16)) subtractor_1 (.a(Input1), .b(multiplexer_1_out), .out(subtractor_1_out));  // open: bin, bout
  Adder #(.width(16)) adder_1 (.a(multiplexer_1_out), .b(Input1), .out(adder_1_out));  // open: cin, cout
  Multiplexer #(.select(3), .width(16), .enable("false")) multiplexer_2 (
    .in0(adder_1_out), .in1(subtractor_1_out), .in2(and_1_out), .in3(or_1_out), .in4(xor_1_out),
    .in5(shifter_2_out), .in6(shifter_1_out), .in7(mod_1_res), .out(Output), .sel(e2));
endmodule

module DecodeIR (
  input  [31:0] IR,
  output Store,
  output Load,
  output CALL,
  output RET,
  output CTRL,
  output WriteReg,
  output [2:0] GetOp,
  output [15:0] JMPAddress
);

  and and_1 (CTRL, IR[0], IR[1]);
  // AND_Gate and_2 has open pins: in0=IR[0], in1=IR[1], out=open
  and and_3 (WriteReg, ~IR[0], ~IR[1]);  // AND_Gate
  Comparator #(.width(3)) comparator_1 (.a(IR[4:2]), .b(3'b101), .eq(CALL));  // open: gt, lt
  Comparator #(.width(3)) comparator_2 (.a(IR[4:2]), .b(3'b110), .eq(RET));  // open: gt, lt
  assign JMPAddress = CTRL ? IR[31:16] : 16'bz;  // Controlled_Buffer controlled_buffer_1

  assign GetOp = IR[4:2];
  assign Load = 1'b0;
  assign Store = 1'b0;
endmodule

module GetAddr (
  input  [15:0] PC,
  input  Load,
  input  Store,
  input  Fetch,
  output [15:0] Addr
);


  assign Addr = PC;
endmodule

module GetCst (
  input  [31:0] IR,
  output [15:0] Cst,
  output Imm
);


  assign Cst = IR[31:16];
  assign Imm = IR[5];
endmodule

module RamCtrl (
  input  Clock,
  input  Exec,
  input  Fetch,
  input  Load,
  input  Store,
  output MemLoad,
  output MemStore
);

  wire and_1_out;

  and and_1 (and_1_out, Exec, Load);
  and and_2 (MemStore, Exec, Clock, Store);
  or or_1 (MemLoad, Fetch, and_1_out);
endmodule

module Registres (
  input  [15:0] IN,
  input  WriteReg,
  input  [2:0] SR1,
  input  [2:0] SR2,
  input  [2:0] DR,
  input  Clock,
  input  Reset,
  output [15:0] R0,
  output [15:0] R1,
  output [15:0] R2,
  output [15:0] R3,
  output [15:0] OUT_SR1,
  output [15:0] OUT_SR2,
  output [15:0] OUT_DR,
  output [15:0] R4,
  output [15:0] R5,
  output [15:0] R6,
  output [15:0] R7
);

  wire decoder_1_out0, decoder_1_out1, decoder_1_out2, decoder_1_out3, decoder_1_out4, decoder_1_out5,
       decoder_1_out6, decoder_1_out7;
  wire [15:0] controlled_buffer_1_out;

  assign controlled_buffer_1_out = WriteReg ? IN : 16'bz;  // Controlled_Buffer controlled_buffer_1
  Decoder #(.select(3), .enable("false")) decoder_1 (
    .out0(decoder_1_out0), .out1(decoder_1_out1), .out2(decoder_1_out2), .out3(decoder_1_out3),
    .out4(decoder_1_out4), .out5(decoder_1_out5), .out6(decoder_1_out6), .out7(decoder_1_out7), .sel(DR));
  Register #(.width(16), .trigger("falling")) u_R0 (
    .D(controlled_buffer_1_out), .en(decoder_1_out0), .Q(R0), .clk(Clock), .clr(Reset));
  Register #(.width(16), .trigger("falling")) u_R1 (
    .D(controlled_buffer_1_out), .en(decoder_1_out1), .Q(R1), .clk(Clock), .clr(Reset));
  Register #(.width(16), .trigger("falling")) u_R2 (
    .D(controlled_buffer_1_out), .en(decoder_1_out2), .Q(R2), .clk(Clock), .clr(Reset));
  Register #(.width(16), .trigger("falling")) u_R3 (
    .D(controlled_buffer_1_out), .en(decoder_1_out3), .Q(R3), .clk(Clock), .clr(Reset));
  Register #(.width(16), .trigger("falling")) u_R4 (
    .D(controlled_buffer_1_out), .en(decoder_1_out4), .Q(R4), .clk(Clock), .clr(Reset));
  Register #(.width(16), .trigger("falling")) u_R5 (
    .D(controlled_buffer_1_out), .en(decoder_1_out5), .Q(R5), .clk(Clock), .clr(Reset));
  Register #(.width(16), .trigger("falling")) u_R6 (
    .D(controlled_buffer_1_out), .en(decoder_1_out6), .Q(R6), .clk(Clock), .clr(Reset));
  Register #(.width(16), .trigger("falling")) u_R7 (
    .D(controlled_buffer_1_out), .en(decoder_1_out7), .Q(R7), .clk(Clock), .clr(Reset));
  Multiplexer #(.select(3), .width(16), .enable("false")) multiplexer_1 (
    .in0(R0), .in1(R1), .in2(R2), .in3(R3), .in4(R4), .in5(R5), .in6(R6), .in7(R7), .out(OUT_SR1), .sel(SR1));
  Multiplexer #(.select(3), .width(16), .enable("false")) multiplexer_2 (
    .in0(R0), .in1(R1), .in2(R2), .in3(R3), .in4(R4), .in5(R5), .in6(R6), .in7(R7), .out(OUT_SR2), .sel(SR2));
  Multiplexer #(.select(3), .width(16), .enable("false")) multiplexer_3 (
    .in0(R0), .in1(R1), .in2(R2), .in3(R3), .in4(R4), .in5(R5), .in6(R6), .in7(R7), .out(OUT_DR), .sel(DR));
endmodule

module RegPC (
  input  [15:0] JMP_Address,
  input  Cond,
  input  CTRL,
  input  Clock,
  input  Reset,
  input  CALL,
  input  RET,
  output [15:0] PC,
  output [15:0] Arith
);

  wire and_1_out, FinRet, Pile_emptystack;
  wire [15:0] adder_1_out, multiplexer_1_out, multiplexer_2_out;

  Multiplexer #(.width(16), .enable("false")) multiplexer_1 (
    .in0(JMP_Address), .in1(Arith), .out(multiplexer_1_out), .sel(RET));
  and and_1 (and_1_out, Cond, CTRL, FinRet);
  Adder #(.width(16)) adder_1 (.a(PC), .b(16'h1), .out(adder_1_out));  // open: cin, cout
  Multiplexer #(.width(16), .enable("false")) multiplexer_2 (
    .in0(adder_1_out), .in1(multiplexer_1_out), .out(multiplexer_2_out), .sel(and_1_out));
  Pile Pile (.PC(PC), .CALL(CALL), .RET(RET), .Clock(Clock), .Reset(Reset), .Out(Arith), .emptyStack(Pile_emptystack));
  nand nand_1 (FinRet, Pile_emptystack, RET);
  Register #(.width(16), .trigger("falling")) u_PC (
    .D(multiplexer_2_out), .Q(PC), .clk(Clock), .clr(Reset));  // open: en

  // Other names for the same wires on the sheet: RETPILE[15:0] = Arith
endmodule

module Seq (
  input  ClockOrig,
  input  reset,
  output Fetch,
  output Exec,
  output Clock
);

  Register #(.width(1), .trigger("falling")) register_1 (
    .D(Fetch), .Q(Exec), .clk(ClockOrig), .clr(reset));  // open: en
  not not_1 (Fetch, Exec);
  buf buffer_1 (Clock, ClockOrig);
endmodule

module Mod (
  input  [15:0] Input1,
  input  [15:0] Input1_2,
  output [15:0] Res
);

  wire [15:0] divider_1_out, multiplier_1_out;

  Divider #(.width(16)) divider_1 (.a(Input1), .b(Input1_2), .out(divider_1_out));  // open: upper, rem
  Multiplier #(.width(16)) multiplier_1 (.a(divider_1_out), .b(Input1_2), .out(multiplier_1_out));  // open: cin, cout
  Subtractor #(.width(16)) subtractor_1 (.a(Input1), .b(multiplier_1_out), .out(Res));  // open: bin, bout
endmodule

module Cond_Crtl (
  input  [15:0] Reg1,
  input  [15:0] Reg2,
  input  [2:0] GetOp,
  output Cond
);

  wire comparator_1_eq, comparator_1_gt, comparator_1_lt, not_1_out;

  Comparator #(.width(16)) comparator_1 (
    .a(Reg2), .b(Reg1), .gt(comparator_1_gt), .eq(comparator_1_eq), .lt(comparator_1_lt));
  not not_1 (not_1_out, comparator_1_eq);
  Multiplexer #(.select(3), .enable("false")) multiplexer_1 (
    .in0(1'b1), .in1(comparator_1_eq), .in2(not_1_out), .in3(comparator_1_lt), .in4(comparator_1_gt),
    .in5(1'b1), .in6(1'b1), .out(Cond), .sel(GetOp));  // open: in7
endmodule

module Pile (
  input  [15:0] PC,
  input  CALL,
  input  RET,
  input  Clock,
  input  Reset,
  output emptyStack,
  output [15:0] Out
);

  wire [15:0] controlled_buffer_1_out, multiplexer_1_out, multiplexer_2_out, SP_1, SP_1_t, SP_q;

  Multiplexer #(.width(16), .enable("false")) multiplexer_1 (
    .in0(SP_1), .in1(SP_1_t), .out(multiplexer_1_out), .sel(RET));
  assign controlled_buffer_1_out = CALL ? 16'h1 : 16'bz;  // Controlled_Buffer controlled_buffer_1
  Register #(.width(16)) SP (.D(multiplexer_1_out), .Q(SP_q), .clk(Clock), .clr(Reset));  // open: en
  Subtractor #(.width(16)) subtractor_1 (.a(SP_q), .b(16'h1), .out(SP_1_t));  // open: bin, bout
  Adder #(.width(16)) adder_1 (.a(SP_q), .b(controlled_buffer_1_out), .out(SP_1));  // open: cin, cout
  Multiplexer #(.width(16), .enable("false")) multiplexer_2 (
    .in0(SP_q), .in1(SP_1_t), .out(multiplexer_2_out), .sel(RET));
  Comparator #(.width(16)) comparator_1 (.a(SP_q), .b({16{1'b0}}), .eq(emptyStack));  // open: gt, lt
  RAM #(.addrWidth(16), .dataWidth(16), .bus("separate")) ram_1 (
    .addr(multiplexer_2_out), .din(PC), .data(Out), .str(CALL), .clk(Clock), .ld(RET), .clr(Reset));  // open: sel

  // Notes on the sheet:
  //   Out: pull=up
endmodule

module Pile2 (
  input  [15:0] PC,
  input  CALL,
  input  RET,
  input  Clock,
  input  Reset,
  output [15:0] Out
);

  wire [15:0] adder_1_out, controlled_buffer_1_out, controlled_buffer_2_out, ram_1_data, SP_q,
       subtractor_1_out, undriven;

  assign controlled_buffer_1_out = RET ? 16'h1 : 16'bz;  // Controlled_Buffer controlled_buffer_1
  Subtractor #(.width(16)) subtractor_1 (
    .a(undriven), .b(controlled_buffer_1_out), .out(subtractor_1_out));  // open: bin, bout
  assign controlled_buffer_2_out = CALL ? 16'h1 : 16'bz;  // Controlled_Buffer controlled_buffer_2
  Register #(.width(16)) SP (.D(subtractor_1_out), .Q(SP_q), .clr(Reset));  // open: en, clk
  Adder #(.width(16)) adder_1 (.a(SP_q), .b(controlled_buffer_2_out), .out(adder_1_out));  // open: cin, cout
  RAM #(.addrWidth(16), .dataWidth(16), .bus("separate")) ram_1 (
    .addr(adder_1_out), .din(PC), .data(ram_1_data), .str(CALL), .clk(Clock), .ld(RET), .clr(Reset));  // open: sel
  assign Out = RET ? ram_1_data : 16'bz;  // Controlled_Buffer controlled_buffer_3
endmodule
